# Fritzing sketch BesucherZähler (saved by Fritzing 0.9.10b)
circuit board: 5.5cm x 4.5cm

parts:
  microSD1 = MicroSD Card Module
  bt = female pin header, 2 pins [form="♀ (female)"]
  bt-led = female pin header, 2 pins [form="♀ (female)"]
  7seg = female pin header, 5 pins [form="♀ (female)"]
  battery5V = female pin header, 2 pins [form="♀ (female)"]
  A1 = Esp32-c3 super mini

nets:
  N1: microSD1.GND, bt.pin1, bt-led.pin1, 7seg.pin2, battery5V.pin2, A1.Pin_15
  N2: microSD1.VCC, 7seg.pin1, battery5V.pin1, A1.Pin_16
  N3: microSD1.MISO, A1.Pin_8
  N4: microSD1.MOSI, A1.Pin_7
  N5: microSD1.SCK, A1.Pin_6
  N6: microSD1.CS, A1.Pin_5
  N7: bt.pin2, A1.Pin_11
  N8: bt-led.pin2, A1.Pin_12
  N9: 7seg.pin3, A1.Pin_13
  N10: 7seg.pin4, A1.Pin_1
  N11: 7seg.pin5, A1.Pin_2

notes:
  BesucherZählerV1
  bt
  7seg
  led
  SD-Karte
  ESP32C3
  +
  -

custom parts:
  MicroSD Card Module: A common microSD card module.
  Esp32-c3 super mini: ESP32-C3 Development Board ESP32 SuperMini Development Board ESP32 Development Board WiFi Bluetooth.
