# Fritzing sketch BesucherZählerS2MiniV2.2GroundFill (saved by Fritzing 0.9.10b)
circuit board: 5.5cm x 4.5cm

parts:
  bt-led = female pin header, 2 pins [form="♀ (female)"]
  A2 = Wemos S2 Mini [part_number="WeMos D1 Mini Lite"]
  bt = female pin header, 2 pins [form="♀ (female)"]
  battery5V = female pin header, 2 pins [form="♀ (female)"]
  microSD1 = female pin header, 6 pins [form="♀ (female)"]
  7seg = female pin header, 5 pins [form="♀ (female)"]

nets:
  GND: bt-led.pin1, A2.Pin_18, A2.Pin_26, bt.pin1, battery5V.pin2, microSD1.pin1, 7seg.pin2
  BT_LED: bt-led.pin2, A2.Pin_5
  BT_PIN: A2.Pin_2, bt.pin2
  VCC: A2.Pin_17, battery5V.pin1, microSD1.pin2, 7seg.pin1
  7S_PIN: A2.Pin_19, 7seg.pin3
  7S_CLK: A2.Pin_20, 7seg.pin4
  7S_CS: A2.Pin_21, 7seg.pin5
  SD_CS: A2.Pin_22, microSD1.pin6
  SD_SCK: A2.Pin_23, microSD1.pin5
  SD_MOSI: A2.Pin_24, microSD1.pin4
  SD_MISO: A2.Pin_32, microSD1.pin3

notes:
  BesucherZählerV2
  bt
  7seg
  led
  +
  -
  SD
  ESP32 S2 Mini

custom parts:
  Wemos S2 Mini: A mini wifi board based on the ESP32-S2FN4R2.
